# Fritzing sketch HW_DIAGRAM_COMP_SLAVE (saved by Fritzing 1.0.4)

parts:
  Part1 = Adafruit AS7341  # not connected
  Part2 = Barometric Pressure Sensor - BMP180 Breakout (GY-68)
  A1 = DHT22 module
  M1 = DOIT Esp32 DevKit v1 (30 pins long, 11 pins width) [part_number=ESP32S-PIN30]
  DS1 = DS18B20 1-Wire Temperature Sensor [part_number=DS18B20]
  Part3 = BH1750
  M2 = DOIT Esp32 DevKit v1 (30 pins long, 11 pins width) [part_number=ESP32S-PIN30]
  M3 = INA3221 Triple Channel Current/Voltage Monitor Module [part_number=CJMCU-3221]
  R1 = Resistor [tolerance=±5% power=0.25W resistance=220 package=THT]  # not connected

nets (from the breadboard view):
  3V3: Part2.SDA, M1.3V3, Part3.VCC
  GND: A1.GND, M1.GND
  N1: A1.DAT, M1.D13
  N2: M1.D4, DS1.DQ
  N3: M1.D21, Part3.SDA
  N4: M1.D22, Part3.SCL
  N5: M2.3V3, M3.TC
  N6: M2.GND, M3.WAR
  N7: M2.D21, M3.PV
  N8: M2.D22, M3.CRI

custom parts:
  DHT22 module: DHT22 module. Pins GND VCC Data.
  DOIT Esp32 DevKit v1 (30 pins long, 11 pins width): The DOIT Esp32 DevKit v1 is one of the development board created by DOIT to evaluate the ESP-WROOM-32 module. It is based on the ESP32 microcontroller that boasts Wifi, Bluetooth, Ethernet and Low Power support all in a single chip. (vanepp) made breadboard work, adjusted pin numbering and labels and reduced size of schematic and cleaned up pcb. This chip is 30pins long (2 x15) and 11 pins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
  BH1750: Light Sensor
  INA3221 Triple Channel Current/Voltage Monitor Module: INA3221 Triple Channel Current/Voltage Monitor Module Links: INA3221 product information
